// Logisim project thing.circ as structural Verilog: 1 circuit, main circuit main
module main (
  output out_1,
  output out_2,
  output out_3,
  output out_4,
  output out_5,
  output out_6,
  output out_7,
  output out_8
);

  wire and_1_out, and_2_out, CLK_out, comparator_1_eq, counter_1_carry, counter_2_carry, counter_3_carry,
       counter_4_carry, counter_6_carry, d_ff_1_q, decoder_1_out0, decoder_1_out1, decoder_1_out2,
       demultiplexer_1_out0, demultiplexer_1_out1, demultiplexer_1_out2, demultiplexer_1_out3,
       demultiplexer_1_out4, demultiplexer_1_out5, demultiplexer_1_out6, demultiplexer_1_out7, not_1_out,
       or_1_out, shift_register_1_out, t_ff_1_q;
  wire [1:0] counter_5_q;
  wire [2:0] counter_4_q;
  wire [3:0] counter_2_q;

  Clock CLK (.out(CLK_out));
  Counter #(.width(4), .max('hf)) counter_1 (.carry(counter_1_carry), .clk(CLK_out));  // open: load, D, count, Q, clr
  Shift_Register #(.length(16)) shift_register_1 (
    .shift(counter_1_carry), .in(shift_register_1_out), .clk(CLK_out), .out(shift_register_1_out));  // open: load, clr, d0, q0, d1, q1, d2, q2, d3, q3, d4, q4, d5, q5, d6, q6, d7, q7, d8, q8, d9, q9, d10, q10, d11, q11, d12, q12, d13, q13, d14, q14, d15, q15
  not not_1 (not_1_out, shift_register_1_out);
  T_Flip_Flop t_ff_1 (
    .clk(CLK_out), .T(not_1_out), .Q(t_ff_1_q), .reset(counter_6_carry), .en(decoder_1_out0));  // open: Qn, preset
  Counter #(.width(4), .max('hf)) counter_2 (
    .count(decoder_1_out1), .Q(counter_2_q), .carry(counter_2_carry), .clk(CLK_out), .clr(counter_6_carry));  // open: load, D
  Counter #(.width(3), .max('h7)) counter_3 (
    .carry(counter_3_carry), .clk(t_ff_1_q), .clr(counter_3_carry));  // open: load, D, count, Q
  and and_1 (and_1_out, counter_3_carry, decoder_1_out0);
  or or_1 (or_1_out, and_1_out, and_2_out);
  Comparator #(.width(4), .mode("unsigned")) comparator_1 (
    .a(counter_2_q), .b(4'b0111), .eq(comparator_1_eq));  // open: gt, lt
  Counter #(.width(3), .max('h7)) counter_4 (
    .Q(counter_4_q), .carry(counter_4_carry), .clk(counter_2_carry), .clr(counter_6_carry));  // open: load, D, count
  and and_2 (and_2_out, counter_4_carry, shift_register_1_out);
  Decoder #(.select(2)) decoder_1 (
    .out0(decoder_1_out0), .out1(decoder_1_out1), .out2(decoder_1_out2), .sel(counter_5_q));  // open: out3, en
  Counter #(.width(2), .max('h2)) counter_5 (
    .Q(counter_5_q), .clk(or_1_out), .clr(counter_6_carry));  // open: load, D, count, carry
  D_Flip_Flop d_ff_1 (
    .clk(CLK_out), .D(decoder_1_out1), .Q(d_ff_1_q), .reset(counter_6_carry));  // open: Qn, preset, en
  Counter #(.width(4), .max('hb)) counter_6 (
    .count(decoder_1_out2), .carry(counter_6_carry), .clk(CLK_out), .clr(counter_6_carry));  // open: load, D, Q
  Demultiplexer #(.select(3), .disabled(0)) demultiplexer_1 (
    .out0(demultiplexer_1_out0), .out1(demultiplexer_1_out1), .out2(demultiplexer_1_out2),
    .out3(demultiplexer_1_out3), .out4(demultiplexer_1_out4), .out5(demultiplexer_1_out5),
    .out6(demultiplexer_1_out6), .out7(demultiplexer_1_out7), .in(d_ff_1_q), .sel(counter_4_q));  // open: en
  D_Flip_Flop d_ff_2 (
    .clk(comparator_1_eq), .D(shift_register_1_out), .Q(out_1), .en(demultiplexer_1_out0));  // open: Qn, preset, reset
  D_Flip_Flop d_ff_3 (
    .clk(comparator_1_eq), .D(shift_register_1_out), .Q(out_2), .en(demultiplexer_1_out1));  // open: Qn, preset, reset
  D_Flip_Flop d_ff_4 (
    .clk(comparator_1_eq), .D(shift_register_1_out), .Q(out_3), .en(demultiplexer_1_out2));  // open: Qn, preset, reset
  D_Flip_Flop d_ff_5 (
    .clk(comparator_1_eq), .D(shift_register_1_out), .Q(out_4), .en(demultiplexer_1_out3));  // open: Qn, preset, reset
  D_Flip_Flop d_ff_6 (
    .clk(comparator_1_eq), .D(shift_register_1_out), .Q(out_5), .en(demultiplexer_1_out4));  // open: Qn, preset, reset
  D_Flip_Flop d_ff_7 (
    .clk(comparator_1_eq), .D(shift_register_1_out), .Q(out_6), .en(demultiplexer_1_out5));  // open: Qn, preset, reset
  D_Flip_Flop d_ff_8 (
    .clk(comparator_1_eq), .D(shift_register_1_out), .Q(out_7), .en(demultiplexer_1_out6));  // open: Qn, preset, reset
  D_Flip_Flop d_ff_9 (
    .clk(comparator_1_eq), .D(shift_register_1_out), .Q(out_8), .en(demultiplexer_1_out7));  // open: Qn, preset, reset

  // Notes on the sheet:
  //   |
  //   |
  //   READSTATE
  //   inner clock
  //   state
  //   LSB
  //   MSB
endmodule
