// Logisim project thing2.circ as structural Verilog: 1 circuit, main circuit main
module main (
  output VLD
);

  wire and_1_out, and_2_out, and_3_out, CLK_out, clock_1_out, clock_2_out, comparator_1_eq, counter_1_carry,
       counter_2_carry, counter_4_carry, counter_5_carry, counter_6_carry, counter_7_carry, decoder_1_out0,
       decoder_1_out1, decoder_1_out2, decoder_1_out3, demultiplexer_1_out0, demultiplexer_1_out1,
       demultiplexer_1_out2, demultiplexer_1_out3, demultiplexer_1_out4, demultiplexer_1_out5,
       demultiplexer_1_out6, demultiplexer_1_out7, not_1_out, or_1_out, shift_register_1_out;
  wire [1:0] counter_3_q;
  wire [2:0] counter_7_q;
  wire [3:0] counter_2_q;
  wire [7:0] register_1_q;

  Clock CLK (.out(CLK_out));
  Counter #(.max('hf), .width(4)) counter_1 (
    .carry(counter_1_carry), .clk(CLK_out));  // open: load, D, count, Q, up, clr
  Shift_Register #(.length(16)) shift_register_1 (
    .shift(counter_1_carry), .in(shift_register_1_out), .clk(CLK_out), .out(shift_register_1_out));  // open: load, clr, d0, q0, d1, q1, d2, q2, d3, q3, d4, q4, d5, q5, d6, q6, d7, q7, d8, q8, d9, q9, d10, q10, d11, q11, d12, q12, d13, q13, d14, q14, d15, q15
  // Probe on shift_register_1_out
  not not_1 (not_1_out, shift_register_1_out);
  Clock clock_1 (.out(clock_1_out));
  and and_1 (and_1_out, and_3_out, counter_7_carry);
  and and_2 (and_2_out, decoder_1_out0, not_1_out);
  Counter #(.max('hf), .width(4)) counter_2 (
    .count(decoder_1_out2), .Q(counter_2_q), .carry(counter_2_carry), .clk(clock_1_out), .clr(counter_4_carry));  // open: load, D, up
  Counter #(.max('h3), .width(2)) counter_3 (.Q(counter_3_q), .clk(or_1_out));  // open: load, D, count, carry, up, clr
  or or_1 (or_1_out, and_2_out, and_1_out, counter_5_carry, counter_4_carry);
  Comparator #(.mode("unsigned"), .width(4)) comparator_1 (
    .a(counter_2_q), .b(4'b1000), .eq(comparator_1_eq));  // open: gt, lt
  Decoder #(.select(2)) decoder_1 (
    .out0(decoder_1_out0), .out1(decoder_1_out1), .out2(decoder_1_out2), .out3(decoder_1_out3),
    .sel(counter_3_q));  // open: en
  Counter #(.max('h7), .ongoal("stay"), .width(3)) counter_4 (
    .count(decoder_1_out3), .carry(counter_4_carry), .clk(clock_2_out), .clr(decoder_1_out0));  // open: load, D, Q, up
  D_Flip_Flop d_ff_1 (.clk(decoder_1_out3), .D(1'b1), .Q(VLD), .reset(counter_6_carry));  // open: Qn, preset
  and and_3 (and_3_out, comparator_1_eq, decoder_1_out2);
  Counter #(.max('h10), .width(5)) counter_5 (
    .count(decoder_1_out1), .carry(counter_5_carry), .clk(clock_2_out), .clr(decoder_1_out2));  // open: load, D, Q, up
  Clock clock_2 (.out(clock_2_out));
  Counter #(.max('h1), .width(1)) counter_6 (
    .carry(counter_6_carry), .clk(clock_2_out));  // open: load, D, count, Q, up, clr
  Counter #(.max('h7), .width(3)) counter_7 (
    .Q(counter_7_q), .carry(counter_7_carry), .clk(counter_2_carry), .clr(counter_4_carry));  // open: load, D, count, up
  // Probe on and_3_out
  Demultiplexer #(.enable("true"), .select(3)) demultiplexer_1 (
    .out0(demultiplexer_1_out0), .out1(demultiplexer_1_out1), .out2(demultiplexer_1_out2),
    .out3(demultiplexer_1_out3), .out4(demultiplexer_1_out4), .out5(demultiplexer_1_out5),
    .out6(demultiplexer_1_out6), .out7(demultiplexer_1_out7), .sel(counter_7_q));  // open: in, en
  Register #(.width(1)) register_1 (
    .D(shift_register_1_out), .en(demultiplexer_1_out0), .Q(register_1_q[0]), .clk(and_3_out));  // open: clr
  Register #(.width(1)) register_2 (
    .D(shift_register_1_out), .en(demultiplexer_1_out1), .Q(register_1_q[1]), .clk(and_3_out));  // open: clr
  Register #(.width(1)) register_3 (
    .D(shift_register_1_out), .en(demultiplexer_1_out2), .Q(register_1_q[2]), .clk(and_3_out));  // open: clr
  Register #(.width(1)) register_4 (
    .D(shift_register_1_out), .en(demultiplexer_1_out3), .Q(register_1_q[3]), .clk(and_3_out));  // open: clr
  Register #(.width(1)) register_5 (
    .D(shift_register_1_out), .en(demultiplexer_1_out4), .Q(register_1_q[4]), .clk(and_3_out));  // open: clr
  Register #(.width(1)) register_6 (
    .D(shift_register_1_out), .en(demultiplexer_1_out5), .Q(register_1_q[5]), .clk(and_3_out));  // open: clr
  Register #(.width(1)) register_7 (
    .D(shift_register_1_out), .en(demultiplexer_1_out6), .Q(register_1_q[6]), .clk(and_3_out));  // open: clr
  Register #(.width(1)) register_8 (
    .D(shift_register_1_out), .en(demultiplexer_1_out7), .Q(register_1_q[7]), .clk(and_3_out));  // open: clr
  // Probe on register_1_q

  // Notes on the sheet:
  //   |
  //   |
  //   START BIT
  //   8 READ
  //   MIDBIT?
  //   STATE MACHINE
  //   WRITE ALLOWED
  //   ADDR
endmodule
